# Fritzing sketch talking_clock (saved by Fritzing 1.0.6)
breadboards: 1

parts:
  Mod1 = Raspberry Pi Pico
  S3 = Pushbutton [package="[SMD]"]
  S4 = Pushbutton [package="[SMD]"]
  S5 = Pushbutton [package="[SMD]"]
  Part1 = RTC DS3231
  microSD1 = MicroSD Card Module
  Part2 = Adafruit MAX98357A I2S 3W Class D Amplifier [part_number="Adafruit #3006"]

nets:
  GND: Mod1.pin_3, Mod1.pin_8, Mod1.pin_13, Mod1.pin_18, Mod1.pin_23, Mod1.pin_28, Mod1.pin_33, Mod1.pin_38, Mod1.pin_42, S3.Pin_3, S3.Pin_4, S4.Pin_3, S4.Pin_4, S5.Pin_3, S5.Pin_4, Part1.GND, Part1.SDA, microSD1.GND, Part2.GND
  N1: Mod1.pin_4, Part1.SCL
  N2: Mod1.pin_14, Part2.DIN
  N3: Mod1.pin_15, Part2.BCLK
  N4: Mod1.pin_16, Part2.LRCLK
  N5: Mod1.pin_17, Part2.GAIN
  N6: Mod1.pin_21, microSD1.MISO
  N7: Mod1.pin_22, microSD1.CS
  N8: Mod1.pin_24, microSD1.SCK
  N9: Mod1.pin_25, microSD1.MOSI
  N10: Mod1.pin_40, microSD1.VCC
  N11: S3.Pin_1, S3.Pin_2
  N12: S4.Pin_1, S4.Pin_2
  N13: S5.Pin_1, S5.Pin_2
  VCC: Part1.VCC, Part2.VIN

custom parts:
  Raspberry Pi Pico: Raspberry Pi Pico. Based around the RP2040 microcontroller the Pico is a low cost microcontroller device bringing Raspberry Pi quality, cost, and easy of use to the microcontroller space. Jan 2021, Split part in to two versions: tht (this one) and SMD. This one will drill holes for a .1 in header in pcb to allow plugging in the module as well as providing pads to solder the module to the top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
  RTC DS3231: DS3231 with akku
  Adafruit MAX98357A I2S 3W Class D Amplifier: Listen to this good news - we now have an all in one digital audio amp breakout board that works incredibly well with the Raspberry Pi! If you're looking for an easy and low cost way to get you digital sound files bumpin' then the MAX08357 I2S Amp Breakout is for you. It takes standard I2S digital audio input and, not only decodes it into analog, but also amplifies it directly into a speaker.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
